// Logisim project main.circ as structural Verilog: 3 circuits, main circuit main
module main (
);

  wire clock_1_out, hours_1_dout, hours_1_ledout, hours_2_dout, hours_2_ledout, hours_3_dout, hours_3_ledout,
       hours_4_dout, hours_4_ledout, hours_5_dout, hours_5_ledout, minutes_1_dout, minutes_1_ledout,
       minutes_2_dout, minutes_2_ledout, minutes_3_dout, minutes_3_ledout, minutes_4_dout, minutes_4_ledout,
       minutes_5_dout, minutes_5_ledout, minutes_6_dout, minutes_6_ledout, minutes_7_dout, minutes_7_ledout,
       minutes_8_dout, minutes_8_ledout, minutes_9_dout, minutes_9_ledout, minutes_10_dout,
       minutes_10_ledout, not_1_out, transistor_1_out;

  LED led_1 (.in(minutes_1_ledout));
  minutes minutes_1 (
    .clk(clock_1_out), .dIn(not_1_out), .LedOut(minutes_1_ledout), .clr(transistor_1_out),
    .dOut(minutes_1_dout));
  not not_1 (not_1_out, clock_1_out);
  LED led_2 (.in(hours_1_ledout));
  LED led_3 (.in(hours_2_ledout));
  hours hours_1 (
    .clk(transistor_1_out), .dIn(hours_2_dout), .LedOut(hours_1_ledout), .clr(hours_4_dout),
    .dOut(hours_1_dout));
  hours hours_2 (
    .clk(transistor_1_out), .dIn(minutes_10_dout), .LedOut(hours_2_ledout), .clr(hours_4_dout),
    .dOut(hours_2_dout));
  LED led_4 (.in(minutes_4_ledout));
  LED led_5 (.in(minutes_2_ledout));
  minutes minutes_2 (
    .clk(clock_1_out), .dIn(minutes_1_dout), .LedOut(minutes_2_ledout), .clr(transistor_1_out),
    .dOut(minutes_2_dout));
  LED led_6 (.in(hours_5_ledout));
  LED led_7 (.in(hours_3_ledout));
  hours hours_3 (
    .clk(transistor_1_out), .dIn(hours_1_dout), .LedOut(hours_3_ledout), .clr(hours_4_dout),
    .dOut(hours_3_dout));
  LED led_8 (.in(minutes_3_ledout));
  minutes minutes_3 (
    .clk(clock_1_out), .dIn(minutes_4_dout), .LedOut(minutes_3_ledout), .clr(transistor_1_out),
    .dOut(minutes_3_dout));
  minutes minutes_4 (
    .clk(clock_1_out), .dIn(minutes_2_dout), .LedOut(minutes_4_ledout), .clr(transistor_1_out),
    .dOut(minutes_4_dout));
  LED led_9 (.in(hours_4_ledout));
  hours hours_4 (
    .clk(transistor_1_out), .dIn(hours_5_dout), .LedOut(hours_4_ledout), .clr(hours_4_dout),
    .dOut(hours_4_dout));
  hours hours_5 (
    .clk(transistor_1_out), .dIn(hours_3_dout), .LedOut(hours_5_ledout), .clr(hours_4_dout),
    .dOut(hours_5_dout));
  LED led_10 (.in(minutes_7_ledout));
  LED led_11 (.in(minutes_5_ledout));
  minutes minutes_5 (
    .clk(clock_1_out), .dIn(minutes_3_dout), .LedOut(minutes_5_ledout), .clr(transistor_1_out),
    .dOut(minutes_5_dout));
  Clock clock_1 (.out(clock_1_out));
  LED led_12 (.in(minutes_6_ledout));
  minutes minutes_6 (
    .clk(clock_1_out), .dIn(minutes_7_dout), .LedOut(minutes_6_ledout), .clr(transistor_1_out),
    .dOut(minutes_6_dout));
  minutes minutes_7 (
    .clk(clock_1_out), .dIn(minutes_5_dout), .LedOut(minutes_7_ledout), .clr(transistor_1_out),
    .dOut(minutes_7_dout));
  LED led_13 (.in(minutes_8_ledout));
  LED led_14 (.in(minutes_9_ledout));
  minutes minutes_8 (
    .clk(clock_1_out), .dIn(minutes_9_dout), .LedOut(minutes_8_ledout), .clr(transistor_1_out),
    .dOut(minutes_8_dout));
  minutes minutes_9 (
    .clk(clock_1_out), .dIn(minutes_6_dout), .LedOut(minutes_9_ledout), .clr(transistor_1_out),
    .dOut(minutes_9_dout));
  LED led_15 (.in(minutes_10_ledout));
  minutes minutes_10 (
    .clk(clock_1_out), .dIn(minutes_8_dout), .LedOut(minutes_10_ledout), .clr(transistor_1_out),
    .dOut(minutes_10_dout));
  Transistor #(.\type ("n"), .gate("br")) transistor_1 (
    .in(minutes_10_dout), .out(transistor_1_out), .gate(clock_1_out));
endmodule

module minutes (
  input  clk,
  input  dIn,
  input  clr,
  output LedOut,
  output dOut
);

  D_Flip_Flop d_ff_1 (.clk(clk), .D(dIn), .Q(dOut), .reset(clr));  // open: Qn, preset, en

  assign LedOut = dOut;
endmodule

module hours (
  input  clk,
  input  dIn,
  input  clr,
  output LedOut,
  output dOut
);

  D_Flip_Flop d_ff_1 (.clk(clk), .D(dIn), .Q(dOut), .reset(clr));  // open: Qn, preset, en

  assign LedOut = dOut;
endmodule
